# Fritzing sketch DippingMechanismSchematic (saved by Fritzing 0.8.5b)
breadboards: 2

parts:
  Part1 = Arduino Uno (Rev3) - ICSP
  U1 = LCD-16X2 [package=lcd-16x2]
  U2 = POT [package=trim_pot]
  R1 = Resistor [tolerance=±5% resistance=220 package=THT]
  S1 = Pushbutton [package="[THT]"]
  S2 = Pushbutton [package="[THT]"]
  S3 = Pushbutton [package="[THT]"]
  S4 = Pushbutton [package="[THT]"]
  M1 = Stepper Motor - Unipolar  # not connected
  Part2 = EasyDriver_v44

nets:
  N1: Part1.D8, S3.Pin_3, S3.Pin_4
  N2: Part1.D9_PWM, S4.Pin_3, S4.Pin_4
  N3: Part1.D11_PWM/MOSI, U1.E
  N4: Part1.D12/MISO, U1.RS
  N5: Part1.D0/RX, Part2.DIR
  N6: Part1.D1/TX, Part2.STEP
  N7: Part1.D2, U1.DB7
  N8: Part1.D3_PWM, U1.DB6
  N9: Part1.D4, U1.DB5
  N10: Part1.D5_PWM, U1.DB4
  N11: Part1.D6_PWM, S1.Pin_1, S1.Pin_2
  N12: Part1.D7, S2.Pin_1, S2.Pin_2
  5V: Part1.5V, U1.VDD, R1.Pin_0, Part2.VCC
  GND: Part1.GND, U1.VSS, U1.R_W, U1.K, S1.Pin_3, S1.Pin_4, S2.Pin_3, S2.Pin_4, S3.Pin_1, S3.Pin_2, S4.Pin_1, S4.Pin_2, Part2.GND
  N13: U1.VO, U2.E
  N14: U1.A, R1.Pin_1
